// Logisim project ALS_18bce245.circ as structural Verilog: 4 circuits, main circuit main
module main (
  input  [4:0] S4_S3_S2_S1_S0,
  input  Cin,
  input  [3:0] A,
  input  [3:0] B,
  input  S5,
  input  Serial_I_p,
  output Cout,
  output [3:0] Ouput,
  output Overflow_bit
);

  wire [3:0] airthmetic_unit_1_answer, logic_unit_1_output, multiplexer_1_out, shift_unit_1_p5;

  Multiplexer #(.width(4)) multiplexer_1 (.in0(B), .in1(A), .out(multiplexer_1_out), .sel(S5));  // open: en
  Airthmetic_Unit airthmetic_unit_1 (
    .Selection_Bits(S4_S3_S2_S1_S0[3:2]), .Cin(Cin), .A(A), .B(B), .Cout(Cout),
    .Answer(airthmetic_unit_1_answer));
  Logic_Unit logic_unit_1 (.Selection_Bits(S4_S3_S2_S1_S0[3:2]), .A(A), .B(B), .Output(logic_unit_1_output));
  // Shift_Unit shift_unit_1: pin names not known; wires that end beside it: S4_S3_S2_S1_S0[4:2], Serial_I_p, multiplexer_1_out, Serial_I_p, shift_unit_1_p5, Overflow_bit
  Multiplexer #(.select(2), .width(4)) multiplexer_2 (
    .in0(airthmetic_unit_1_answer), .in1(logic_unit_1_output), .in2(shift_unit_1_p5), .in3(4'b0000),
    .out(Ouput), .sel(S4_S3_S2_S1_S0[1:0]));  // open: en

  // Notes on the sheet:
  //   Selection I/p
  //   Legend for Arithmetic Unit
  //   S3,S2,Cin
  //   ------------------------------
  //   Add
  //   0  0  0
  //   0  0  1
  //   0  1  0
  //   0  1  1
  //   Subtract
  //   1  0  0
  //   1  0  1
  //   1  1  0
  //   1  1  1
  //   Arithmetic Unit
  //   Logical Unit
  //   Shift Unit
  //   Add with carry
  //   Subtract with borrow
  //   Transfer A
  //   Increment A
  //   Decrement A
  //   Transfer A
  //   TIRTH PATEL (18BCE245)
  //   S3,S2
  //   00
  //   01
  //   10
  //   11
  //   Legend for Logic Unit
  //   ----------------------------------
  //   AND operation
  //   OR Operation
  //   XOR Operation
  //   NOT Operation
  //   Legend for Shift Unit
  //   S4,S3,S2
  //   000
  //   001
  //   010
  //   011
  //   100
  //   101
  //   0 0
  //   0 1
  //   1 0
  //   ----------------------------------
  //   Logical Shift Left
  //   Logical Shift RIght
  //   Circular Shift Left
  //   Circular Shift RIght
  //   Arithmetic Shift Left
  //   Arithmetic Shift Right
  //   --------------------------------------
  //   Legend
  //   for S0 and S1
  //   Arithmetic Unit
  //   Logical Unit
  //   Shift Unit
endmodule

module Shift_Unit (
  input  in_1,
  input  [2:0] Selection_BIts,
  input  [3:0] A,
  input  in_4,
  output [3:0] Answer,
  output OverFlow
);

  wire and_1_out, not_1_out, xor_1_out;

  Multiplexer #(.select(3)) multiplexer_1 (
    .in0(in_1), .in1(A[1]), .in2(A[3]), .in3(A[1]), .in4(1'b0), .in5(A[1]), .in6(1'b0), .in7(1'b0),
    .out(Answer[0]), .sel(Selection_BIts));  // open: en
  Multiplexer #(.select(3)) multiplexer_2 (
    .in0(A[0]), .in1(A[2]), .in2(A[0]), .in3(A[2]), .in4(A[0]), .in5(A[2]), .in6(1'b0), .in7(1'b0),
    .out(Answer[1]), .sel(Selection_BIts));  // open: en
  Multiplexer #(.select(3)) multiplexer_3 (
    .in0(A[1]), .in1(A[3]), .in2(A[1]), .in3(A[3]), .in4(A[1]), .in5(A[3]), .in6(1'b0), .in7(1'b0),
    .out(Answer[2]), .sel(Selection_BIts));  // open: en
  Multiplexer #(.select(3)) multiplexer_4 (
    .in0(A[2]), .in1(in_4), .in2(A[2]), .in3(A[0]), .in4(A[2]), .in5(A[3]), .in6(1'b0), .in7(1'b0),
    .out(Answer[3]), .sel(Selection_BIts));  // open: en
  not not_1 (not_1_out, Selection_BIts[0]);
  and and_1 (and_1_out, Selection_BIts[2], not_1_out);
  xor xor_1 (xor_1_out, A[3], A[2]);
  and and_2 (OverFlow, and_1_out, xor_1_out);

  // Notes on the sheet:
  //   Serial I/p Logical Right
  //   Serial I/p Logical Left
  //   S4,S3,S2
  //   000
  //   001
  //   010
  //   011
  //   100
  //   101
  //   Legend
  //   ----------------------------------
  //   Logical Shift Left
  //   Logical Shift RIght
  //   Circular Shift Left
  //   Circular Shift RIght
  //   Arithmetic Shift Left
  //   Arithmetic Shift Right
  //   --------------------------------------
endmodule

module Airthmetic_Unit (
  input  [1:0] Selection_Bits,
  input  Cin,
  input  [3:0] A,
  input  [3:0] B,
  output [3:0] Answer,
  output Cout
);

  wire [3:0] multiplexer_1_out, not_1_out, not_2_out;

  assign not_1_out = ~B;  // NOT_Gate not_1, 4 bits wide
  assign not_2_out = ~4'b0000;  // NOT_Gate not_2, 4 bits wide
  Multiplexer #(.select(2), .width(4)) multiplexer_1 (
    .in0(B), .in1(not_1_out), .in2(4'b0000), .in3(not_2_out), .out(multiplexer_1_out), .sel(Selection_Bits));  // open: en
  Adder #(.width(4)) adder_1 (.a(A), .b(multiplexer_1_out), .out(Answer), .cin(Cin), .cout(Cout));

  // Notes on the sheet:
  //   Legend
  //   S3,S2,Cin
  //   ------------------------------
  //   0  0  0
  //   0  0  1
  //   0  1  0
  //   0  1  1
  //   1  0  0
  //   1  0  1
  //   1  1  0
  //   1  1  1
  //   Add
  //   Add with carry
  //   Subtract with borrow
  //   Subtract
  //   Transfer A
  //   Increment A
  //   Decrement A
  //   Transfer A
endmodule

module Logic_Unit (
  input  [1:0] Selection_Bits,
  input  [3:0] A,
  input  [3:0] B,
  output [3:0] Output
);

  wire [3:0] and_1_out, not_1_out, or_1_out, xor_1_out;

  assign and_1_out = A & B;  // AND_Gate and_1, 4 bits wide
  assign or_1_out = A | B;  // OR_Gate or_1, 4 bits wide
  assign xor_1_out = A ^ B;  // XOR_Gate xor_1, 4 bits wide
  assign not_1_out = ~A;  // NOT_Gate not_1, 4 bits wide
  Multiplexer #(.select(2), .width(4)) multiplexer_1 (
    .in0(and_1_out), .in1(or_1_out), .in2(xor_1_out), .in3(not_1_out), .out(Output), .sel(Selection_Bits));  // open: en

  // Notes on the sheet:
  //   Legend
  //   S3,S2
  //   00
  //   01
  //   10
  //   11
  //   AND operation
  //   OR Operation
  //   XOR Operation
  //   NOT Operation
endmodule
